// Logisim project Zadanie1_SasinkovaNikolaLogisim.circ as structural Verilog: 1 circuit, main circuit main
module main (
  input  A,
  input  B,
  input  C,
  input  D,
  output Z_KNF,
  output Y_zad,
  output Z_zad,
  output Y_DNF,
  output Z_DNF,
  output Y_KNF
);

  wire A_D_out, A_nC_out, and_2_out, B_D_out, B_nC_out, nand_1_out, nor_1_out, not_1_out, not_2_out,
       not_3_out, not_4_out, not_5_out, not_6_out, not_7_out, not_8_out, not_9_out, or_1_out, or_2_out,
       or_3_out, or_4_out, or_5_out;

  not not_1 (not_1_out, D);
  not not_2 (not_2_out, A);
  not not_3 (not_3_out, B);
  not not_4 (not_4_out, D);
  not not_5 (not_5_out, C);
  not not_6 (not_6_out, A);
  not not_7 (not_7_out, C);
  not not_8 (not_8_out, B);
  not not_9 (not_9_out, D);
  and and_1 (Z_KNF, not_8_out, not_9_out, C);
  nor nor_1 (nor_1_out, A, B);
  nand nand_1 (nand_1_out, C, not_1_out);
  or or_1 (or_1_out, B, D);
  and and_2 (and_2_out, not_2_out, not_3_out, C, not_4_out);
  and A_nC (A_nC_out, A, not_5_out);
  and A_D (A_D_out, A, D);
  and B_nC (B_nC_out, B, not_5_out);
  and B_D (B_D_out, B, D);
  or or_2 (or_2_out, A, B, C);
  or or_3 (or_3_out, A, B, not_9_out);
  or or_4 (or_4_out, not_6_out, not_7_out, D);
  or or_5 (or_5_out, not_8_out, not_7_out, D);
  or or_6 (Y_DNF, and_2_out, A_nC_out, A_D_out, B_nC_out, B_D_out);
  and and_3 (Z_DNF, not_3_out, C, not_4_out);
  and and_4 (Y_KNF, or_2_out, or_3_out, or_4_out, or_5_out);
  xor xor_1 (Y_zad, nor_1_out, nand_1_out);
  nor nor_2 (Z_zad, nand_1_out, or_1_out);

  // Notes on the sheet:
  //   !(A+B)
  //   !(C.!D)
  //   (B+D)
  //   (!A.!B.C.!D)
  //   (A+B+C)
  //   (A+B+!D)
  //   (!A+!C+D)
  //   (!B+!C+D)
  //   (!B.C.!D)
  //   (!A.!B.C.!D)+(A.!C)+(A.D)+(B.!C)+(B.D)
  //   (!B.C.!D)
  //   !(A+B).!(!(C.!D))+!(!(A+B)).!(C.!D)
  //   !((!(C.!D))+(B+D))
  //   (A+B+C).(A+B+!D).(!A+!C+D).(!B+!C+D)
endmodule
